# Fritzing sketch pi_i2s (1) (saved by Fritzing 0.9.3b)

parts:
  Part1 = Adafruit I2S Mic - SPH0645 [part_number="Adafruit #3421"]
  Part3 = Adafruit MAX98357A I2S 3W Class D Amplifier [part_number="Adafruit #3006"]
  Part4 = 16 NeoPixel Ring [part_number=1463]
  Part5 = Adafruit Ultimate GPS HAT [part_number="Adafruit #2324"]
  S1 = Momentary Switch [package=ksa_sealed_tac_switch]
  Part6 = Adafruit DS1307 RTC Breakout [part_number="Adafruit #264"]

nets:
  VDD: Part1.VDD, Part5.3.3V
  GND: Part1.GND, Part3.GND, Part4.GND, Part5.GND, S1.4, Part6.GND
  N1: Part1.BCLK, Part3.BCLK, Part5.GPIO18
  N2: Part1.DATA, Part5.GPIO20
  N3: Part1.WS, Part3.LRCLK, Part5.GPIO19
  VIN: Part3.VIN, Part4.VDD, Part5.5.0V, Part6.VCC
  N4: Part3.DIN, Part5.GPIO21
  N5: Part4.OUT, Part5.SPI_MOSI
  N6: Part5.SDA, Part6.SDA
  N7: Part5.SCL, Part6.SCL
  N8: Part5.GPIO23, S1.3

custom parts:
  Adafruit I2S Mic - SPH0645: For many microcontrollers, adding audio input is easy with one of our analog microphone breakouts. But as you get to bigger and better microcontrollers and microcomputers, you'll find that you don't always have an analog input, or maybe you want to avoid the noise that can seep in with an analog mic system. Once you get past 8-bit micros, you will often find an I2S peripheral, that can take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
  Adafruit MAX98357A I2S 3W Class D Amplifier: Listen to this good news - we now have an all in one digital audio amp breakout board that works incredibly well with the Raspberry Pi! If you're looking for an easy and low cost way to get you digital sound files bumpin' then the MAX08357 I2S Amp Breakout is for you. It takes standard I2S digital audio input and, not only decodes it into analog, but also amplifies it directly into a speaker.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
  16 NeoPixel Ring: 16 ultra bright smart LED NeoPixels are arranged in a circle with 1.75" (44.5mm) outer diameter. The rings are 'chainable' - connect the output pin of one to the input pin of another. Use only one microcontroller pin to control as many as you can chain together! Each LED is addressable as the driver chip is inside the LED. Each one has ~18mA constant current drive so the color will be very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
  Adafruit Ultimate GPS HAT: It's 10PM, do you know where your Raspberry Pi is? If you had this GPS HAT, you would! This new HAT from Adafruit adds our celebrated Ultimate GPS on it, so you can add precision time and location to your Raspberry Pi Model A+, B+, or Pi 2. Does not work with the Pi 3 at this time Here's the low-down on the GPS module: -165 dBm sensitivity, 10 Hz updates, 66 channels Only 20mA current draw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
  Adafruit DS1307 RTC Breakout: This is a great battery-backed real time clock (RTC) that allows your microcontroller project to keep track of time even if it is reprogrammed, or if the power is lost. Perfect for datalogging, clock-building, time stamping, timers and alarms, etc. The DS1307 is the most popular RTC - but it requires 5V power to work (although we've used it with 5V power and 3.3V logic successfully) PCB &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
